// Logisim project Instructions.circ as structural Verilog: 1 circuit, main circuit main
module main (
  input  in_1,
  input  in_2,
  input  in_3,
  input  in_4,
  input  in_5
);

  wire AC_ON, adder_1_cout, and_2_out, AR_ON, CLK, CLR_SC, D0T4, D0T5, D0T6, D1T4, D1T5, D1T6, D4T4, D4T5,
       decoder_1_out0, decoder_1_out1, decoder_1_out2, decoder_1_out3, decoder_2_out0, decoder_2_out1,
       decoder_2_out4, decoder_2_out7, DR_ON, or_1_out, or_6_out, RAM_LOAD_ON, register_2_q, T4, T5, T6;
  wire [2:0] counter_6_q, S0_out;
  wire [11:0] bit_extender_1_out, bit_extender_2_out, counter_1_q, counter_2_q;
  wire [15:0] adder_1_out, and_1_out, bit_extender_3_out, bit_extender_4_out, counter_4_q, counter_5_q,
       DECODE_INS, multiplexer_1_out, multiplexer_2_out, ram_1_data;

  Clock clock_1 (.out(CLK));
  Bit_Extender #(.in_width(16), .out_width(12)) bit_extender_1 (.in(multiplexer_1_out), .out(bit_extender_1_out));
  Bit_Extender #(.in_width(16), .out_width(12)) bit_extender_2 (.in(multiplexer_1_out), .out(bit_extender_2_out));
  Counter #(.width(12), .max('hfff)) counter_1 (
    .load(AR_ON), .D(bit_extender_1_out), .count(in_3), .Q(counter_1_q), .clk(CLK), .clr(in_3));  // open: carry
  Counter #(.width(12), .max('hfff)) counter_2 (
    .load(D4T4), .D(bit_extender_2_out), .count(or_1_out), .Q(counter_2_q), .clk(CLK));  // open: carry, clr
  Counter #(.width(16), .max('hffff)) counter_3 (
    .load(or_1_out), .D(multiplexer_1_out), .count(in_3), .Q(DECODE_INS), .clk(CLK));  // open: carry, clr
  Counter #(.width(16), .max('hffff)) counter_4 (
    .load(AC_ON), .D(multiplexer_2_out), .count(in_1), .Q(counter_4_q), .clk(CLK));  // open: carry, clr
  Counter #(.width(16), .max('hffff)) counter_5 (
    .load(DR_ON), .D(multiplexer_1_out), .count(in_1), .Q(counter_5_q), .clk(CLK));  // open: carry, clr
  assign bit_extender_3_out = {{4{1'b0}}, counter_1_q};  // Bit_Extender bit_extender_3
  buf or_1 (or_1_out, decoder_1_out1);  // OR_Gate
  or or_2 (DR_ON, D0T4, D1T4);
  or or_3 (CLR_SC, D1T6, D4T5, D0T6);
  RAM #(.addrWidth(12), .dataWidth(16), .bus("separate")) ram_1 (
    .addr(counter_1_q), .data(ram_1_data), .str(in_5), .clk(CLK), .ld(RAM_LOAD_ON));  // open: din, sel, clr
  assign bit_extender_4_out = {{4{1'b0}}, counter_2_q};  // Bit_Extender bit_extender_4
  or or_4 (AR_ON, decoder_1_out0, and_2_out, decoder_1_out2);
  Counter #(.width(3), .max('h7)) counter_6 (.Q(counter_6_q), .clk(CLK), .clr(CLR_SC));  // open: load, D, count, carry
  Decoder #(.select(3), .enable("false")) decoder_1 (
    .out0(decoder_1_out0), .out1(decoder_1_out1), .out2(decoder_1_out2), .out3(decoder_1_out3), .out4(T4),
    .out5(T5), .out6(T6), .sel(counter_6_q));  // open: out7
  assign and_1_out = counter_4_q & counter_5_q;  // AND_Gate and_1, 16 bits wide
  Adder #(.width(16)) adder_1 (.a(counter_4_q), .b(counter_5_q), .out(adder_1_out), .cout(adder_1_cout));  // open: cin
  Register #(.width(1)) register_1 (.D(adder_1_cout), .clk(CLK));  // open: en, Q, clr
  Multiplexer #(.select(3), .width(16), .enable("false")) multiplexer_1 (
    .in1(bit_extender_3_out), .in2(bit_extender_4_out), .in3(counter_5_q), .in5(DECODE_INS),
    .in7(ram_1_data), .out(multiplexer_1_out), .sel(S0_out));  // open: in0, in4, in6
  or or_5 (RAM_LOAD_ON, decoder_1_out1, DR_ON, decoder_1_out3);
  Multiplexer #(.width(16)) multiplexer_2 (
    .in0(and_1_out), .in1(adder_1_out), .out(multiplexer_2_out), .sel(D1T5), .en(or_6_out));
  Decoder #(.select(3), .enable("false")) decoder_2 (
    .out0(decoder_2_out0), .out1(decoder_2_out1), .out4(decoder_2_out4), .out7(decoder_2_out7),
    .sel(DECODE_INS[14:12]));  // open: out2, out3, out5, out6
  or S2 (S0_out[2], decoder_1_out3, decoder_1_out1, decoder_1_out2, DR_ON);
  or S0 (S0_out[0], decoder_1_out3, decoder_1_out1, D4T4, decoder_1_out2, DR_ON);
  or or_6 (or_6_out, decoder_2_out0, decoder_2_out1);
  Register #(.width(1)) register_2 (.D(DECODE_INS[15]), .Q(register_2_q), .clk(CLK));  // open: en, clr
  or S1 (S0_out[1], decoder_1_out0, decoder_1_out1, decoder_1_out3, DR_ON);
  and and_2 (and_2_out, ~decoder_2_out7, register_2_q, decoder_1_out3);  // AND_Gate
  and and_3 (D1T4, decoder_2_out1, T4);
  and and_4 (D4T4, T4, decoder_2_out4);
  and and_5 (D4T5, decoder_2_out4, T5);
  and and_6 (D0T4, decoder_2_out0, T4);
  and and_7 (D0T5, decoder_2_out0, T5);
  and and_8 (D0T6, decoder_2_out0, T6);
  and and_9 (D1T5, decoder_2_out1, T5);
  and and_10 (D1T6, decoder_2_out1, T6);
  or or_7 (AC_ON, D0T5, D1T5);

  // Other names for the same wires on the sheet: RAM_STORE_ON = in_5

  // Notes on the sheet:
  //   AR
  //   PC
  //   IR
  //   AC
  //   DR
  //   E-FlipFlop
  //   Indirect Bit
endmodule
